# Fritzing sketch Lights (saved by Fritzing 0.6.2b)
breadboards: 2

parts:
  Netduino1 = Netduino Plus
  LED1 = white LED - 5mm [package="5 mm [THT]"]
  K1 = Relay [part_number=FRS1B-S package=THT]
  K2 = Relay [part_number=FRS1B-S package=THT]
  K3 = Relay [part_number=FRS1B-S package=THT]
  K4 = Relay [part_number=FRS1B-S package=THT]
  LED2 = white LED - 5mm [package="5 mm [THT]"]
  LED3 = white LED - 5mm [package="5 mm [THT]"]
  LED4 = white LED - 5mm [package="5 mm [THT]"]
  R4 = Resistor [tolerance=±5% resistance=1 package=THT]
  R5 = Resistor [tolerance=±5% resistance=1 package=THT]
  R6 = Resistor [tolerance=±5% resistance=1 package=THT]
  R7 = Resistor [tolerance=±5% resistance=1 package=THT]

nets:
  N1: Netduino1.D7_RTS1, K4.COIL2
  N2: Netduino1.D6_PWM1, K3.COIL2
  N3: Netduino1.D5_PWM0, K2.COIL2
  N4: Netduino1.D4_CS0, K1.COIL2
  N5: Netduino1.+5V, LED1.cathode, LED2.cathode, LED3.cathode, LED4.cathode
  N6: Netduino1.GND, K1.COIL1, K1.C1, K1.C2, K2.COIL1, K2.C1, K2.C2, K3.COIL1, K3.C1, K3.C2, K4.COIL1, K4.C1, K4.C2
  N7: LED1.anode, R7.Pin_1
  N8: K1.B, R7.Pin_0
  N9: K2.B, R6.Pin_0
  N10: K3.B, R5.Pin_0
  N11: K4.B, R4.Pin_0
  N12: LED2.anode, R6.Pin_1
  N13: LED3.anode, R5.Pin_1
  N14: LED4.anode, R4.Pin_1
